// Logisim project CPU.circ as structural Verilog
module _1M (
  input  I,
  input  S,
  output O
);

  wire _1_out, _2_out, _4_out;

  nand _1 (_1_out, I, S);
  nand _2 (_2_out, _1_out, S);
  nand _3 (O, _1_out, _4_out);
  nand _4 (_4_out, O, _2_out);
endmodule

module _8M (
  input  in_1,
  input  [7:0] in_2,
  output [7:0] out_3
);

  _1M u_1m_1 (.O(out_3[0]), .S(in_1), .I(in_2[0]));
  _1M u_1m_2 (.O(out_3[1]), .S(in_1), .I(in_2[1]));
  _1M u_1m_3 (.O(out_3[2]), .S(in_1), .I(in_2[2]));
  _1M u_1m_4 (.O(out_3[3]), .S(in_1), .I(in_2[3]));
  _1M u_1m_5 (.O(out_3[4]), .S(in_1), .I(in_2[4]));
  _1M u_1m_6 (.O(out_3[5]), .S(in_1), .I(in_2[5]));
  _1M u_1m_7 (.O(out_3[6]), .S(in_1), .I(in_2[6]));
  _1M u_1m_8 (.O(out_3[7]), .S(in_1), .I(in_2[7]));
endmodule

module _8Register (
  input  in_1,
  input  [7:0] in_2,
  input  in_3,
  output [7:0] out_4
);

  wire [7:0] n8m_1_out_3;

  _8M u_8m_1 (.in_1(in_1), .in_2(in_2), .out_3(n8m_1_out_3));
  enabler enabler_1 (.in_1(n8m_1_out_3), .in_2(in_3), .out_3(out_4));
endmodule

module enabler (
  input  [7:0] in_1,
  input  in_2,
  output [7:0] out_3
);

  and and_1 (out_3[0], in_2, in_1[0]);
  and and_2 (out_3[1], in_2, in_1[1]);
  and and_3 (out_3[2], in_2, in_1[2]);
  and and_4 (out_3[3], in_2, in_1[3]);
  and and_5 (out_3[4], in_2, in_1[4]);
  and and_6 (out_3[5], in_2, in_1[5]);
  and and_7 (out_3[6], in_2, in_1[6]);
  and and_8 (out_3[7], in_2, in_1[7]);
endmodule

module Bus_Copy (
  input  in_1,
  input  in_2,
  input  in_3,
  input  in_4,
  input  [7:0] in_5,
  output [7:0] out_6,
  output [7:0] out_7,
  output [7:0] out_8
);

  wire and_1_out, not_1_out, not_2_out;

  not not_1 (not_1_out, in_4);
  not not_2 (not_2_out, in_3);
  and and_1 (and_1_out, not_1_out, not_2_out);
  assign out_8 = and_1_out ? in_5 : 8'bz;  // Controlled_Buffer in_Buff
  _8Register RA (.out_4(out_6), .in_2(out_8), .in_1(in_1), .in_3(in_3));
  assign out_8 = in_3 ? out_6 : 8'bz;  // Controlled_Buffer out_BuffA
  _8Register RB (.out_4(out_7), .in_2(out_8), .in_1(in_2), .in_3(in_4));
  assign out_8 = in_4 ? out_7 : 8'bz;  // Controlled_Buffer out_BuffB
endmodule
